# Fritzing sketch Water level sensor Fritzing sketch real (saved by Fritzing 0.9.3b)
breadboards: 1

parts:
  Arduino_Uno = Arduino Uno (Rev3)
  U1 = RELAY [package=relay-t9a]
  Q1 = NPN-Transistor [part_number=2N3904 package="TO92 [THT]"]
  R1 = Resistor [tolerance=±5% resistance=1k package=THT]
  S1 = Square Pushbutton
  S2 = Square Pushbutton
  R2 = Resistor [tolerance=±5% resistance=1k package=THT]
  R3 = Resistor [tolerance=±5% resistance=1k package=THT]
  D1 = Rectifier Diode [part_number=1N4001 package="300 mil [THT]"]
  IC1 = Voltage Regulator [part_number=7805 package=78xxl]
  Q4 = NPN-Transistor [part_number=2N3904 package="TO92 [THT]"]
  R6 = Resistor [tolerance=±5% resistance=1k package=THT]
  R4 = Resistor [tolerance=±5% resistance=1k package=THT]
  Pump_indicator = smd LED [color="Green (565nm)" package="0603 [SMD]"]
  Q5 = NPN-Transistor [part_number=2N3904 package="TO92 [THT]"]
  R7 = Resistor [tolerance=±5% resistance=1k package=THT]
  R8 = Resistor [tolerance=±5% resistance=1k package=THT]
  Lower_Switch_indicator = smd LED [color="Red (633nm)" package="0603 [SMD]"]
  Q6 = NPN-Transistor [part_number=2N3904 package="TO92 [THT]"]
  R9 = Resistor [tolerance=±5% resistance=1k package=THT]
  R10 = Resistor [tolerance=±5% resistance=1k package=THT]
  Upper_Switch_indicator = smd LED [color="Blue (525nm)" package="0603 [SMD]"]
  C5 = Electrolytic Capacitor [capacitance=1000µF package="300 mil [THT, electrolytic]"]
  D9 = Rectifier Diode [part_number=1N4001 package="300 mil [THT]"]
  D10 = Rectifier Diode [part_number=1N4001 package="300 mil [THT]"]
  D11 = Rectifier Diode [part_number=1N4001 package="300 mil [THT]"]
  D12 = Rectifier Diode [part_number=1N4001 package="300 mil [THT]"]
  U4 = Transformer [part_number="220/12V, 2A" package=transformer]
  V6 = AC Power [voltage=220 frequency=50]
  IC2 = Voltage Regulator [part_number=7812 package=78xxl]

nets:
  N1: Arduino_Uno.A0, R10.Pin_0
  N2: Arduino_Uno.A1, R7.Pin_0
  N3: Arduino_Uno.A2, R6.Pin_0
  GND: Arduino_Uno.GND, Q1.E, R2.Pin_1, R3.Pin_1, IC1.GND, R4.Pin_1, R8.Pin_1, R9.Pin_1, C5.-, D10.cathode, D11.anode, U4.3, IC2.GND
  N4: Arduino_Uno.D2, S1.leg0, R2.Pin_0
  N5: Arduino_Uno.D3_PWM, S2.leg0
  N6: Arduino_Uno.D4, R1.Pin_0
  N7: Arduino_Uno.VIN, D1.cathode, IC1.IN, IC2.OUT
  N8: U1.COIL2, Q1.C, D1.anode
  from water pump: U1.MAIN
  to water pump: U1.NO
  N9: Q1.B, R1.Pin_1
  N10: S1.leg1, S2.leg1, IC1.OUT, Pump_indicator.anode, Lower_Switch_indicator.anode, Upper_Switch_indicator.anode
  N11: Q4.E, R4.Pin_0
  N12: Q4.B, R6.Pin_1
  N13: Q4.C, Pump_indicator.cathode
  N14: Q5.E, R8.Pin_0
  N15: Q5.B, R7.Pin_1
  N16: Q5.C, Lower_Switch_indicator.cathode
  N17: Q6.E, R9.Pin_0
  N18: Q6.B, R10.Pin_1
  N19: Q6.C, Upper_Switch_indicator.cathode
  N20: C5.+, D9.cathode, D11.cathode, IC2.IN
  N21: D9.anode, D12.cathode, U4.4
  N22: D10.anode, D12.anode
  N23: U4.1, V6.V+
  N24: U4.2, V6.V-
